# Fritzing sketch scheme (saved by Fritzing 0.9.3b)
breadboards: 1

parts:
  Part1 = Arduino Nano (Rev3.0) (ICSP)
  Part2 = Bluetooth HC-05 Macho
  Part3 = ws2812b [package="smd 2812b"]
  R1 = Resistor [tolerance=±5% resistance=1k package=THT]
  C2 = Electrolytic Capacitor [capacitance=22µF package="0405 [SMD, electrolytic]"]
  R2 = Resistor [tolerance=±5% resistance=10k package="0402 [SMD]"]
  R3 = Resistor [tolerance=±5% resistance=10k package="0402 [SMD]"]

nets:
  GND: Part1.GND, Part2.GND, Part3.VSS, C2.-, R3.Pin_1
  N1: Part1.D2, R2.Pin_1
  N2: Part1.D3, Part2.TXD
  N3: Part1.D9, R1.Pin_0
  5V: Part1.5V, Part2.VCC, Part3.VDD, C2.+
  N4: Part2.RXD, R2.Pin_0, R3.Pin_0
  N5: Part3.DIN, R1.Pin_1
